# Fritzing sketch TS-570_controler_01 (saved by Fritzing 0.9.6b)
breadboards: 1

parts:
  DS2Y-5-DC5V1 = DS2Y-5-DC5V [part_number=DS2Y-5-DC5V]
  DS2Y-5-DC5V2 = DS2Y-5-DC5V [part_number=DS2Y-5-DC5V]
  J1 = Camdenboss CTB0158-3 [part_number=CTB0158-3 package=THT]
  J2 = Camdenboss CTB0158-2 [part_number=CTB0158-2 package=THT]
  J3 = Camdenboss CTB0158-2 [part_number=CTB0158-2 package=THT]
  J4 = Camdenboss CTB0158-3 [part_number=CTB0158-3 package=THT]
  J5 = Camdenboss CTB0158-2 [part_number=CTB0158-2 package=THT]
  D1 = Rectifier Diode [part_number=1N4001 package="300 mil [THT]"]
  D2 = Rectifier Diode [part_number=1N4001 package="300 mil [THT]"]
  LED1 = LED - 5mm [color="Blue (430nm)" current=0.02 package="5 mm [THT]"]
  R1 = Resistor [tolerance=±5% power=0.25 resistance=6.8k package=THT]

nets:
  N1: DS2Y-5-DC5V1.8_N.O., J1.pin2
  N2: DS2Y-5-DC5V1.4_COM, J4.pin2
  N3: DS2Y-5-DC5V1.1_+, DS2Y-5-DC5V2.1_+, D1.cathode, D2.cathode, R1.Pin_0
  N4: DS2Y-5-DC5V1.16_-, DS2Y-5-DC5V2.16_-, J3.pin1, D1.anode, LED1.cathode
  N5: DS2Y-5-DC5V1.13_COM, J1.pin1
  N6: DS2Y-5-DC5V1.9_N.O., J4.pin3
  N7: DS2Y-5-DC5V2.8_N.O., J2.pin1
  N8: DS2Y-5-DC5V2.4_COM, J5.pin2
  N9: DS2Y-5-DC5V2.13_COM, J2.pin2
  N10: DS2Y-5-DC5V2.9_N.O., J5.pin1
  N11: J1.pin3, J4.pin1
  N12: J3.pin2, D2.anode
  N13: LED1.anode, R1.Pin_1
